# Fritzing sketch Sketch (saved by Fritzing 0.8.7b)
breadboards: 1

parts:
  LCD1 = LCD screen
  Part1 = Arduino Uno (Rev3)
  R1 = Resistor [tolerance=±5% resistance=3.3k package=THT]
  R2 = Resistor [tolerance=±5% resistance=10k package=THT]
  R3 = Temperature Sensor (Thermistor) [thermistor_type=NTC package=THT]
  R4 = Photocell (LDR) [package=THT]
  R5 = Resistor [tolerance=±5% resistance=1k package=THT]
  Part2 = Real Time Clock Module - DS1307 RTC Breakout Board

nets:
  GND: LCD1.VSS, LCD1.R/W, LCD1.LED-, Part1.GND, R1.Pin_0, R2.Pin_0, R5.Pin_0, Part2.GND
  5V: LCD1.VDD, Part1.5V, R3.pin_1, R4.pin_1, Part2.5V
  N1: LCD1.V0, R1.Pin_1
  N2: LCD1.RS, Part1.D7
  N3: LCD1.E, Part1.D8
  N4: LCD1.DB4, Part1.D9_PWM
  N5: LCD1.DB5, Part1.D10_PWM/SS
  N6: LCD1.DB6, Part1.D11_PWM/MOSI
  N7: LCD1.DB7, Part1.D12/MISO
  N8: LCD1.LED+, Part1.D6_PWM
  N9: Part1.A0, R2.Pin_1, R3.pin_0
  N10: Part1.A1, R4.pin_0, R5.Pin_1
  N11: Part1.A4/SDA, Part2.SDA
  N12: Part1.A5/SCL, Part2.SCL
